# Fritzing sketch breadboard (saved by Fritzing 0.9.6b)
breadboards: 1

parts:
  Mod1 = Raspberry Pi Pico
  SEN1 = US-100 Ultrasonic Distance Sensor
  Bauteil1 = Barometric Pressure Sensor - BMP180 Breakout (GY-68)
  Bauteil2 = Adafruit TPL5110 Power Timer [part_number="Adafruit #3435"]
  VCC1 = Battery

nets:
  GND: Mod1.pin_3, Mod1.pin_8, Mod1.pin_13, Mod1.pin_18, Mod1.pin_23, Mod1.pin_28, Mod1.pin_33, Mod1.pin_38, Mod1.pin_42, SEN1.GND, SEN1.GND-2, Bauteil1.GND, Bauteil2.GND, VCC1.-
  N1: Mod1.pin_9, Bauteil1.SDA
  N2: Mod1.pin_10, Bauteil1.SCL
  N3: Mod1.pin_11, SEN1.ECHO
  N4: Mod1.pin_12, SEN1.TRIG
  VCC: Mod1.pin_36, SEN1.VCC, Bauteil1.VCC
  N5: Mod1.pin_39, Bauteil2.PWROUT
  N6: Bauteil2.VDD, VCC1.+

custom parts:
  Raspberry Pi Pico: Raspberry Pi Pico. Based around the RP2040 microcontroller the Pico is a low cost microcontroller device bringing Raspberry Pi quality, cost, and easy of use to the microcontroller space. Jan 2021, Split part in to two versions: tht (this one) and SMD. This one will drill holes for a .1 in header in pcb to allow plugging in the module as well as providing pads to solder the module to the top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
  Adafruit TPL5110 Power Timer: With some development boards, low power usage is an afterthought. Especially when price and usability is the main selling point. So what should you do when its time to turn around and make that project of yours run on a battery or solar? Sure you could try to hot-air that regulator off, or you could jerry-rig a relay. Or, use a 555? Ugh, the options aren't that great. The Adafruit TPL5110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
