# Fritzing sketch stripboard (saved by Fritzing 0.9.6b)
stripboards: 1

parts:
  Mod1 = Raspberry Pi Pico
  Bauteil1 = Barometric Pressure Sensor - BMP180 Breakout (GY-68)
  Bauteil2 = Adafruit TPL5110 Power Timer [part_number="Adafruit #3435"]
  J1 = Screw terminal - 2 pins [package=THT]
  J2 = female pin header, 5 pins [form="♀ (female)"]
  VCC1 = Battery
  SEN1 = US-100 Ultrasonic Distance Sensor

nets:
  GND: Mod1.pin_3, Mod1.pin_8, Mod1.pin_13, Mod1.pin_18, Mod1.pin_23, Mod1.pin_28, Mod1.pin_33, Mod1.pin_38, Bauteil1.GND, Bauteil2.GND, J1.pin2, J2.pin4, J2.pin5, VCC1.-, SEN1.GND, SEN1.GND-2
  Done: Mod1.pin_4, Bauteil2.DONE
  SDA: Mod1.pin_9, Bauteil1.SDA
  SCL: Mod1.pin_10, Bauteil1.SCL
  UART_TX: Mod1.pin_11, J2.pin2, SEN1.TRIG
  UART_RX: Mod1.pin_12, J2.pin3, SEN1.ECHO
  3V3: Mod1.pin_36, Bauteil1.VCC, J2.pin1, SEN1.VCC
  VSYS: Mod1.pin_39, Bauteil2.PWROUT
  N1: Bauteil2.VDD, J1.pin1, VCC1.+

custom parts:
  Raspberry Pi Pico: Raspberry Pi Pico. Based around the RP2040 microcontroller the Pico is a low cost microcontroller device bringing Raspberry Pi quality, cost, and easy of use to the microcontroller space. Jan 2021, Split part in to two versions: tht (this one) and SMD. This one will drill holes for a .1 in header in pcb to allow plugging in the module as well as providing pads to solder the module to the top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
  Adafruit TPL5110 Power Timer: With some development boards, low power usage is an afterthought. Especially when price and usability is the main selling point. So what should you do when its time to turn around and make that project of yours run on a battery or solar? Sure you could try to hot-air that regulator off, or you could jerry-rig a relay. Or, use a 555? Ugh, the options aren't that great. The Adafruit TPL5110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
